# Fritzing sketch Midterm BreadBoard (saved by Fritzing 1.0.2b)
breadboards: 1

parts:
  A1 = Particle - Photon2
  SP1 = SPEAKER [package=pcb_mount_speaker]
  S1 = Pushbutton [package="[THT]"]
  OLED_I2C1 = OLED 128x64 I2C Monochrome Display
  Neopixel1 = Adafruit RBG Smart Neopixel [package="DIP (Dual Inline) [THT]"]
  Part1 = PN532 Elechouse RFID NFC Module V3
  DFRobot_DFPlayer_Mini1 = DFRobot DFPlayer Mini [part_number=DFR0299]
  Grove1 = Grove 4 Digit Display

nets:
  VCC: A1.Pin_2, S1.Pin_1, S1.Pin_2, OLED_I2C1.VDD, Part1.VCC#2, DFRobot_DFPlayer_Mini1.VCC, Grove1.VCC
  N1: A1.Pin_14, DFRobot_DFPlayer_Mini1.TX
  N2: A1.Pin_15, DFRobot_DFPlayer_Mini1.RX
  N3: A1.Pin_17, OLED_I2C1.SDA, Part1.SDA
  N4: A1.Pin_18, OLED_I2C1.SCK, Part1.SCL
  N5: A1.Pin_19, Neopixel1.In
  N6: A1.Pin_20, S1.Pin_3, S1.Pin_4
  N7: A1.Pin_21, Grove1.CLK
  N8: A1.Pin_22, Grove1.DIO
  N9: A1.Pin_26, Neopixel1.+
  N10: SP1.+, DFRobot_DFPlayer_Mini1.SPK_2
  N11: SP1.-, DFRobot_DFPlayer_Mini1.SPK_1
  GND: OLED_I2C1.GND, Neopixel1.G, Part1.GND, DFRobot_DFPlayer_Mini1.GND-1, DFRobot_DFPlayer_Mini1.GND-2, Grove1.GND

custom parts:
  Particle - Photon2: The Photon 2 is a microcontroller and Wi-Fi networking developed by particle. Features: 802.11a/b/g/n Wi-Fi, 2.4 GHz and 5 GHz Integrated PCB antenna Integrated U.FL connector for external antenna Integrated RF switch BLE 5 using same antenna as Wi-Fi Realtek RTL8721DM MCU ARM Cortex M33 CPU, 200 MHz 2048 KB (2 MB) user application maximum size 3072 KB (3 MB) of RAM available to user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
  Pushbutton: A generic pushbutton.
  PN532 Elechouse RFID NFC Module V3: NFC is a popular technology in recent years. We often heard this work while smart phone company such as Samsung or HTC introduces their latest high-end phones. Almost all the high-end phone in the market support NFC. Near field communication (NFC) is a set of standards for smart phones and similar devices to establish radio communication with each other by touching them together or bringing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
