# Fritzing sketch Midterm (saved by Fritzing 1.0.2b)
breadboards: 1

parts:
  A1 = Particle - Photon2
  SP1 = SPEAKER [package=pcb_mount_speaker]
  Button = Pushbutton [package="[THT]"]
  OLED_I2C1 = OLED 128x64 I2C Monochrome Display
  Neopixel = Adafruit RBG Smart Neopixel [package="DIP (Dual Inline) [THT]"]
  NFC_Reader = PN532 Elechouse RFID NFC Module V3
  4_Digit = Grove Button
  DFRobot_DFPlayer_Mini1 = DFRobot DFPlayer Mini [part_number=DFR0299]

nets:
  VCC: A1.Pin_2, Button.Pin_1, Button.Pin_2, OLED_I2C1.VDD, NFC_Reader.VCC#2, 4_Digit.VCC, DFRobot_DFPlayer_Mini1.VCC
  N1: A1.Pin_14, DFRobot_DFPlayer_Mini1.TX
  N2: A1.Pin_15, DFRobot_DFPlayer_Mini1.RX
  N3: A1.Pin_17, OLED_I2C1.SDA, NFC_Reader.SDA
  N4: A1.Pin_18, OLED_I2C1.SCK, NFC_Reader.SCL
  N5: A1.Pin_19, Neopixel.In
  N6: A1.Pin_20, Button.Pin_3, Button.Pin_4
  N7: A1.Pin_26, Neopixel.+
  N8: SP1.+, DFRobot_DFPlayer_Mini1.SPK_2
  N9: SP1.-, DFRobot_DFPlayer_Mini1.SPK_1
  GND: OLED_I2C1.GND, Neopixel.G, NFC_Reader.GND, 4_Digit.GND, DFRobot_DFPlayer_Mini1.GND-1, DFRobot_DFPlayer_Mini1.GND-2

custom parts:
  Particle - Photon2: The Photon 2 is a microcontroller and Wi-Fi networking developed by particle. Features: 802.11a/b/g/n Wi-Fi, 2.4 GHz and 5 GHz Integrated PCB antenna Integrated U.FL connector for external antenna Integrated RF switch BLE 5 using same antenna as Wi-Fi Realtek RTL8721DM MCU ARM Cortex M33 CPU, 200 MHz 2048 KB (2 MB) user application maximum size 3072 KB (3 MB) of RAM available to user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
  Pushbutton: A generic pushbutton.
  PN532 Elechouse RFID NFC Module V3: NFC is a popular technology in recent years. We often heard this work while smart phone company such as Samsung or HTC introduces their latest high-end phones. Almost all the high-end phone in the market support NFC. Near field communication (NFC) is a set of standards for smart phones and similar devices to establish radio communication with each other by touching them together or bringing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
